// Logisim project bfcpu.circ as structural Verilog: 3 circuits, main circuit main
module main (
);

  wire clock_1_out, dipswitch_1_sw1, dipswitch_1_sw2, dipswitch_1_sw3, dipswitch_1_sw4;
  wire [3:0] register4_1_d_out, registerdriver_1_r0;

  Clock clock_1 (.out(clock_1_out));
  DipSwitch #(.number(4)) dipswitch_1 (
    .sw1(dipswitch_1_sw1), .sw2(dipswitch_1_sw2), .sw3(dipswitch_1_sw3), .sw4(dipswitch_1_sw4));
  RegisterDriver registerdriver_1 (
    .RS0(1'b0), .RS1(1'b0), .RS2(1'b0), .EN(dipswitch_1_sw1), .LD(dipswitch_1_sw2), .CE(dipswitch_1_sw3),
    .DEC(dipswitch_1_sw4), .CLC(clock_1_out), .R0(registerdriver_1_r0));  // open: R1, R2, R3, R4, R5, R6, R7
  Register4 register4_1 (
    .EN(registerdriver_1_r0[0]), .LD(registerdriver_1_r0[1]), .UP(registerdriver_1_r0[2]),
    .DN(registerdriver_1_r0[3]), .D_OUT(register4_1_d_out));  // open: D_IN
  Hex_Digit_Display hex_digit_display_1 (.value(register4_1_d_out));  // open: dp
endmodule

module Register4 (
  input  EN,
  input  LD,
  input  UP,
  input  DN,
  input  [3:0] D_IN,
  output [3:0] D_OUT
);

  wire n74193_1_pin11;
  wire [3:0] n74193_1_pin3;

  _74193 u_74193_1 (
    .pin1(D_IN[1]), .pin2(n74193_1_pin3[1]), .pin3(n74193_1_pin3[0]), .pin4(DN), .pin5(UP),
    .pin6(n74193_1_pin3[2]), .pin7(n74193_1_pin3[3]), .pin15(D_IN[0]), .pin11(n74193_1_pin11),
    .pin10(D_IN[2]), .pin9(D_IN[3]));  // open: pin14, pin13, pin12
  not not_1 (n74193_1_pin11, LD);
  assign D_OUT = EN ? n74193_1_pin3 : 4'bz;  // Controlled_Buffer controlled_buffer_1
endmodule

module RegisterDriver (
  input  RS0,
  input  RS1,
  input  RS2,
  input  EN,
  input  LD,
  input  CE,
  input  DEC,
  input  CLC,
  output [3:0] R0,
  output [3:0] R1,
  output [3:0] R2,
  output [3:0] R3,
  output [3:0] R4,
  output [3:0] R5,
  output [3:0] R6,
  output [3:0] R7
);

  wire and_1_out, demultiplexer_1_out0, demultiplexer_1_out1, demultiplexer_2_out0, demultiplexer_2_out1;
  wire [3:2] UP_out;

  Demultiplexer demultiplexer_1 (.out0(demultiplexer_1_out0), .out1(demultiplexer_1_out1), .in(CE), .sel(DEC));
  and and_1 (and_1_out, CE, CLC);
  Demultiplexer demultiplexer_2 (.out0(demultiplexer_2_out0), .out1(demultiplexer_2_out1), .in(and_1_out), .sel(DEC));
  Demultiplexer #(.select(3), .width(4)) demultiplexer_3 (
    .out0(R0), .out1(R1), .out2(R2), .out3(R3), .out4(R4), .out5(R5), .out6(R6), .out7(R7),
    .in({UP_out, LD, EN}), .sel({RS2, RS1, RS0}));
  or UP (UP_out[2], demultiplexer_1_out1, demultiplexer_2_out0);
  or DN (UP_out[3], demultiplexer_1_out0, demultiplexer_2_out1);
endmodule
